// Logisim project mano.circ as structural Verilog: 19 circuits, main circuit main
module main (
  input  ST
);

  wire AC_controller_1_l, and_2_out, AR_controller_1_ar_l, AR_controller_1_plusplus, buffer_1_out,
       Bus_controller_1_s0, Bus_controller_1_s1, Bus_controller_1_s2, clock_1_out, comparator_1_eq, d0, d1,
       d2, d3, d4, d5, d6, DR_Controller_1_l, DR_Controller_1_plusplus, DRZ, IR15, IR_Controller_1_l,
       Mem_controller_1_w, not_1_out, or_1_out, or_2_out, PC_controller_1_l, PC_controller_1_plusplus, t0,
       t1, t2, t3, t4, t5, t6, undriven;
  wire [1:0] ALU_controller_1_mode;
  wire [2:0] T_counter_1_t_out;
  wire [14:0] IR_1_bus_out;
  wire [15:0] AC_1_bus_out, ALU_1_res, AR_1_bus_out, Data_BUS_1_bus_out, DRO, PC_1_bus_out, RAM_1_dout,
       TR_1_bus_out;

  Comparator #(.width(16)) comparator_1 (.a(DRO), .b({16{1'b0}}), .eq(comparator_1_eq));  // open: gt, lt
  and and_1 (DRZ, comparator_1_eq, d5, t6);
  buf buffer_1 (buffer_1_out, DRZ);
  and and_2 (and_2_out, d5, t6);
  Mem_controller Mem_controller_1 (
    .d3(d3), .d2(d2), .t1(t1), .t3(t3), .IR15(IR15), .d0(d0), .t4(t4), .d1(d1), .d5(d5), .d6(d6), .t6(t6),
    .W(Mem_controller_1_w));  // open: R
  not not_1 (not_1_out, Mem_controller_1_w);
  AR_controller AR_controller_1 (
    .t0(t0), .t2(t2), .t3(t3), .IR15(IR15), .t4(t4), .d5(d5), .AR_L(AR_controller_1_ar_l),
    .plusplus(AR_controller_1_plusplus));
  DR_Controller DR_Controller_1 (
    .t4(t4), .d0(d0), .d2(d2), .d3(d3), .d6(d6), .t5(t5), .L(DR_Controller_1_l),
    .plusplus(DR_Controller_1_plusplus));
  ALU_controller ALU_controller_1 (
    .t4(t4), .d2(d2), .d3(d3), .t5(t5), .d0(d0), .mode(ALU_controller_1_mode));  // open: add
  AC_controller AC_controller_1 (.t5(t5), .d0(d0), .d2(d2), .d3(d3), .L(AC_controller_1_l));
  PC_controller PC_controller_1 (
    .t1(t1), .t4(t4), .d4(d4), .t5(t5), .d5(d5), .plusplus(PC_controller_1_plusplus), .L(PC_controller_1_l));
  IR_Controller IR_Controller_1 (.t1(t1), .L(IR_Controller_1_l));
  or or_1 (or_1_out, buffer_1_out, and_2_out);
  or or_2 (or_2_out, PC_controller_1_l, DRZ);
  Clock #(.highDuration(2)) clock_1 (.out(clock_1_out));
  RAM #(.addrWidth(12), .asyncread("true"), .dataWidth(16)) RAM_1 (
    .addr(AR_1_bus_out[11:0]), .we(Mem_controller_1_w), .oe(not_1_out), .clk(clock_1_out),
    .din(Data_BUS_1_bus_out), .dout(RAM_1_dout));
  T_counter T_counter_1 (.En(ST), .CLK(clock_1_out), .clear(or_1_out), .T_out(T_counter_1_t_out));
  AR AR_1 (
    .Bus_in(Data_BUS_1_bus_out), .Load(AR_controller_1_ar_l), .Inc(AR_controller_1_plusplus),
    .CLK(clock_1_out), .Bus_out(AR_1_bus_out));  // open: Clear
  DR DR_1 (
    .Bus_in(Data_BUS_1_bus_out), .Load(DR_Controller_1_l), .Inc(DR_Controller_1_plusplus), .CLK(clock_1_out),
    .Bus_out(DRO));  // open: Clear
  ALU ALU_1 (.A(DRO), .B(AC_1_bus_out), .Mode(ALU_controller_1_mode), .Res(ALU_1_res));  // open: Cin, Add_mode
  AC AC_1 (
    .ALU_in(ALU_1_res), .Load(AC_controller_1_l), .CLK(clock_1_out), .Bus_out(AC_1_bus_out));  // open: Inc, Clear
  PC PC_1 (
    .Bus_in(Data_BUS_1_bus_out), .Load(or_2_out), .Inc(PC_controller_1_plusplus), .CLK(clock_1_out),
    .Clear(undriven), .Bus_out(PC_1_bus_out));
  IR IR_1 (
    .Bus_in(Data_BUS_1_bus_out), .Load(IR_Controller_1_l), .CLK(clock_1_out), .Bus_out({IR15, IR_1_bus_out}));  // open: Inc, Clear
  TR TR_1 (.Bus_in(Data_BUS_1_bus_out), .CLK(clock_1_out), .Bus_out(TR_1_bus_out));  // open: Load, Inc, Clear
  Decoder #(.enable("false"), .select(3)) decoder_1 (
    .out0(t0), .out1(t1), .out2(t2), .out3(t3), .out4(t4), .out5(t5), .out6(t6), .sel(T_counter_1_t_out));  // open: out7
  IR_DCD IR_DCD_1 (
    .opc_in(IR_1_bus_out[14:12]), .d0_Load(d0), .d1_Store(d1), .d2_ADD(d2), .d3_AND(d3), .d4_JUMP(d4),
    .d5_BSA(d5), .d6_ISZ(d6));
  Bus_controller Bus_controller_1 (
    .t0(t0), .t1(t1), .t2(t2), .t3(t3), .IR15(IR15), .t4(t4), .d0(d0), .d1(d1), .t5(t5), .d2(d2), .d3(d3),
    .d4(d4), .d5(d5), .d6(d6), .t6(t6), .s0(Bus_controller_1_s0), .s1(Bus_controller_1_s1),
    .s2(Bus_controller_1_s2));
  Data_BUS Data_BUS_1 (
    .Mem(RAM_1_dout), .AR(AR_1_bus_out), .DR(DRO), .AC(AC_1_bus_out), .PC(PC_1_bus_out),
    .IR({IR15, IR_1_bus_out}), .TR(TR_1_bus_out), .s0(Bus_controller_1_s0), .s1(Bus_controller_1_s1),
    .s2(Bus_controller_1_s2), .Bus_out(Data_BUS_1_bus_out));
endmodule

module ALU (
  input  [15:0] A,
  input  [15:0] B,
  input  Cin,
  input  [1:0] Mode,
  input  Add_mode,
  output [15:0] Res
);

  wire [15:0] adder_1_out, and_1_out, multiplexer_1_out, not_1_out, or_1_out;

  assign not_1_out = ~B;  // NOT_Gate not_1, 16 bits wide
  Multiplexer #(.width(16)) multiplexer_1 (.in0(B), .in1(not_1_out), .out(multiplexer_1_out), .sel(Add_mode));
  assign and_1_out = A & B;  // AND_Gate and_1, 16 bits wide
  assign or_1_out = A | B;  // OR_Gate or_1, 16 bits wide
  Adder #(.width(16)) adder_1 (.a(A), .b(multiplexer_1_out), .out(adder_1_out), .cin(Cin));  // open: cout
  Multiplexer #(.select(2), .width(16)) multiplexer_2 (
    .in0(and_1_out), .in1(or_1_out), .in2(adder_1_out), .in3(A), .out(Res), .sel(Mode));
endmodule

module Data_BUS (
  input  [15:0] Mem,
  input  [15:0] AR,
  input  [15:0] DR,
  input  [15:0] AC,
  input  [15:0] PC,
  input  [15:0] IR,
  input  s0,
  input  [15:0] TR,
  input  s1,
  input  s2,
  output [15:0] Bus_out
);

  Multiplexer #(.select(3), .width(16)) multiplexer_1 (
    .in0(Mem), .in1(AR), .in2(DR), .in3(AC), .in4(PC), .in5(IR), .in6(TR), .out(Bus_out), .sel({s2, s1, s0}));  // open: in7
endmodule

module AR (
  input  [15:0] Bus_in,
  input  Load,
  input  Inc,
  input  CLK,
  input  Clear,
  output [15:0] Bus_out
);

  wire or_1_out;
  wire [11:0] adder_1_out, multiplexer_1_out;

  or or_1 (or_1_out, Load, Inc);
  Multiplexer #(.width(12)) multiplexer_1 (.in0(Bus_in[11:0]), .in1(adder_1_out), .out(multiplexer_1_out), .sel(Inc));
  Register #(.width(12)) register_1 (.D(multiplexer_1_out), .en(or_1_out), .clk(CLK), .Q(Bus_out[11:0]), .clr(Clear));
  Adder #(.width(12)) adder_1 (.a(12'h1), .b(Bus_out[11:0]), .out(adder_1_out));  // open: cin, cout

  assign Bus_out[15:12] = 4'b0000;
endmodule

module DR (
  input  [15:0] Bus_in,
  input  Load,
  input  Inc,
  input  CLK,
  input  Clear,
  output [15:0] Bus_out
);

  wire or_1_out;
  wire [15:0] adder_1_out, multiplexer_1_out;

  or or_1 (or_1_out, Load, Inc);
  Multiplexer #(.width(16)) multiplexer_1 (.in0(Bus_in), .in1(adder_1_out), .out(multiplexer_1_out), .sel(Inc));
  Register #(.width(16)) register_1 (.D(multiplexer_1_out), .en(or_1_out), .clk(CLK), .Q(Bus_out), .clr(Clear));
  Adder #(.width(16)) adder_1 (.a(16'h1), .b(Bus_out), .out(adder_1_out));  // open: cin, cout
endmodule

module AC (
  input  [15:0] ALU_in,
  input  Load,
  input  Inc,
  input  CLK,
  input  Clear,
  output [15:0] Bus_out
);

  wire or_1_out;
  wire [15:0] adder_1_out, multiplexer_1_out;

  or or_1 (or_1_out, Load, Inc);
  Multiplexer #(.width(16)) multiplexer_1 (.in0(ALU_in), .in1(adder_1_out), .out(multiplexer_1_out), .sel(Inc));
  Register #(.width(16)) register_1 (.D(multiplexer_1_out), .en(or_1_out), .clk(CLK), .Q(Bus_out), .clr(Clear));
  Adder #(.width(16)) adder_1 (.a(16'h1), .b(Bus_out), .out(adder_1_out));  // open: cin, cout
endmodule

module PC (
  input  [15:0] Bus_in,
  input  Load,
  input  Inc,
  input  CLK,
  input  Clear,
  output [15:0] Bus_out
);

  wire or_1_out;
  wire [11:0] adder_1_out, multiplexer_1_out;

  or or_1 (or_1_out, Load, Inc);
  Multiplexer #(.width(12)) multiplexer_1 (.in0(Bus_in[11:0]), .in1(adder_1_out), .out(multiplexer_1_out), .sel(Inc));
  Register #(.width(12)) register_1 (.D(multiplexer_1_out), .en(or_1_out), .clk(CLK), .Q(Bus_out[11:0]), .clr(Clear));
  Adder #(.width(12)) adder_1 (.a(12'h1), .b(Bus_out[11:0]), .out(adder_1_out));  // open: cin, cout

  assign Bus_out[15:12] = 4'b0000;
endmodule

module IR (
  input  [15:0] Bus_in,
  input  Load,
  input  Inc,
  input  CLK,
  input  Clear,
  output [15:0] Bus_out
);

  wire or_1_out;
  wire [15:0] adder_1_out, multiplexer_1_out;

  or or_1 (or_1_out, Load, Inc);
  Multiplexer #(.width(16)) multiplexer_1 (.in0(Bus_in), .in1(adder_1_out), .out(multiplexer_1_out), .sel(Inc));
  Register #(.width(16)) register_1 (.D(multiplexer_1_out), .en(or_1_out), .clk(CLK), .Q(Bus_out), .clr(Clear));
  Adder #(.width(16)) adder_1 (.a(16'h1), .b(Bus_out), .out(adder_1_out));  // open: cin, cout
endmodule

module TR (
  input  [15:0] Bus_in,
  input  Load,
  input  Inc,
  input  CLK,
  input  Clear,
  output [15:0] Bus_out
);

  wire or_1_out;
  wire [15:0] adder_1_out, multiplexer_1_out;

  or or_1 (or_1_out, Load, Inc);
  Multiplexer #(.width(16)) multiplexer_1 (.in0(Bus_in), .in1(adder_1_out), .out(multiplexer_1_out), .sel(Inc));
  Register #(.width(16)) register_1 (.D(multiplexer_1_out), .en(or_1_out), .clk(CLK), .Q(Bus_out), .clr(Clear));
  Adder #(.width(16)) adder_1 (.a(16'h1), .b(Bus_out), .out(adder_1_out));  // open: cin, cout
endmodule

module Bus_controller (
  input  t0,
  input  t1,
  input  t2,
  input  t3,
  input  IR15,
  input  t4,
  input  d0,
  input  d1,
  input  t5,
  input  d2,
  input  d3,
  input  d4,
  input  d5,
  input  d6,
  input  t6,
  output s0,
  output s1,
  output s2
);

  wire and_1_out, and_2_out, and_3_out, and_4_out, and_5_out, and_6_out, and_7_out, and_8_out, and_9_out,
       and_10_out, and_11_out, and_12_out, and_13_out, and_14_out;

  and and_1 (and_1_out, t3, IR15);
  and and_2 (and_2_out, t4, d0);
  and and_3 (and_3_out, t4, d1);
  and and_4 (and_4_out, t5, d0);
  and and_5 (and_5_out, d2, t4);
  and and_6 (and_6_out, d3, t4);
  and and_7 (and_7_out, d4, t4);
  and and_8 (and_8_out, d5, t4);
  and and_9 (and_9_out, d5, d0);
  and and_10 (and_10_out, d6, t4);
  and and_11 (and_11_out, d6, t6);
  and and_12 (and_12_out, ~and_5_out, ~and_10_out, ~t1, ~and_8_out, ~t0, ~and_1_out, ~and_4_out, ~and_2_out, ~and_6_out, ~and_11_out);  // AND_Gate
  and and_13 (and_13_out, ~and_5_out, ~and_8_out, ~t0, ~and_7_out, ~t1, ~and_10_out, ~t2, ~and_2_out, ~and_1_out, ~and_6_out, ~and_9_out);  // AND_Gate
  and and_14 (and_14_out, ~and_5_out, ~and_6_out, ~and_1_out, ~and_7_out, ~and_2_out, ~and_10_out, ~and_4_out, ~and_3_out, ~t1, ~and_9_out, ~and_11_out);  // AND_Gate
  or or_1 (s0, t2, and_3_out, and_9_out, and_7_out, and_12_out);
  or or_2 (s1, and_3_out, and_11_out, and_4_out, and_13_out);
  or or_3 (s2, t0, t2, and_8_out, and_14_out);
endmodule

module IR_Controller (
  input  t1,
  output L
);

  buf or_1 (L, t1);  // OR_Gate
endmodule

module AR_controller (
  input  t0,
  input  t2,
  input  t3,
  input  IR15,
  input  t4,
  input  d5,
  output AR_L,
  output plusplus
);

  wire and_1_out;

  and and_1 (and_1_out, t3, IR15);
  and and_2 (plusplus, t4, d5);
  or or_1 (AR_L, t0, t2, and_1_out);
endmodule

module T_counter (
  input  En,
  input  CLK,
  input  clear,
  output [2:0] T_out
);

  wire and_1_out, or_1_out;
  wire [2:0] adder_1_out;

  Register #(.trigger("falling"), .width(3)) register_1 (
    .D(adder_1_out), .en(En), .clk(CLK), .Q(T_out), .clr(or_1_out));
  or or_1 (or_1_out, clear, and_1_out);
  and and_1 (and_1_out, T_out[0], T_out[1], T_out[2]);
  Adder #(.width(3)) adder_1 (.a(3'b001), .b(T_out), .out(adder_1_out));  // open: cin, cout
endmodule

module IR_DCD (
  input  [2:0] opc_in,
  output d0_Load,
  output d1_Store,
  output d2_ADD,
  output d3_AND,
  output d4_JUMP,
  output d5_BSA,
  output d6_ISZ
);

  Decoder #(.enable("false"), .select(3)) decoder_1 (
    .out0(d0_Load), .out1(d1_Store), .out2(d2_ADD), .out3(d3_AND), .out4(d4_JUMP), .out5(d5_BSA),
    .out6(d6_ISZ), .sel(opc_in));  // open: out7
endmodule

module Mem_controller (
  input  d3,
  input  d2,
  input  t1,
  input  t3,
  input  IR15,
  input  d0,
  input  t4,
  input  d1,
  input  d5,
  input  d6,
  input  t6,
  output R,
  output W
);

  wire and_1_out, and_2_out, and_3_out, and_4_out, and_5_out, and_6_out, and_7_out;

  and and_1 (and_1_out, t4, d0);
  and and_2 (and_2_out, d1, t4);
  and and_3 (and_3_out, d5, t4);
  and and_4 (and_4_out, d6, t6);
  and and_5 (and_5_out, t4, d3);
  and and_6 (and_6_out, t4, d2);
  and and_7 (and_7_out, t3, IR15);
  or or_1 (W, and_2_out, and_4_out, and_3_out);
  or or_2 (R, and_6_out, t1, and_5_out, and_7_out, and_1_out);
endmodule

module PC_controller (
  input  t1,
  input  t4,
  input  d4,
  input  t5,
  input  d5,
  output plusplus,
  output L
);

  wire and_1_out, and_2_out;

  and and_1 (and_1_out, t4, d4);
  and and_2 (and_2_out, t5, d5);
  buf or_1 (plusplus, t1);  // OR_Gate
  or or_2 (L, and_1_out, and_2_out);
endmodule

module DR_Controller (
  input  t4,
  input  d0,
  input  d2,
  input  d3,
  input  d6,
  input  t5,
  output L,
  output plusplus
);

  wire and_1_out, and_2_out, and_3_out, and_4_out;

  and and_1 (and_1_out, t4, d0);
  and and_2 (and_2_out, d2, t4);
  and and_3 (and_3_out, d3, t4);
  and and_4 (and_4_out, d6, t4);
  and and_5 (plusplus, d6, t5);
  or or_1 (L, and_1_out, and_2_out, and_3_out, and_4_out);
endmodule

module AC_controller (
  input  t5,
  input  d0,
  input  d2,
  input  d3,
  output L
);

  wire and_1_out, and_2_out, and_3_out;

  and and_1 (and_1_out, t5, d0);
  and and_2 (and_2_out, t5, d2);
  and and_3 (and_3_out, t5, d3);
  or or_1 (L, and_1_out, and_2_out, and_3_out);
endmodule

module ALU_controller (
  input  t4,
  input  d2,
  input  d3,
  input  t5,
  input  d0,
  output [1:0] mode,
  output add
);

  wire and_1_out, and_4_out, or_1_out;
  wire [1:0] and_5_out;
  wire [1:1] and_2_out, and_3_out;

  and and_1 (and_1_out, t5, d0);
  and and_2 (and_2_out[1], t4, d2);
  and and_3 (and_3_out[1], d3, t4);
  and and_4 (and_4_out, d2, t5);
  or or_1 (or_1_out, and_2_out[1], and_4_out);
  Priority_Encoder #(.select(2)) priority_encoder_1 (
    .in0(and_3_out[1]), .in2(or_1_out), .in3(and_1_out), .out(mode), .en_in(1'b1));  // open: in1, gs, en_out
  assign and_5_out = {2{and_2_out[1]}} & 2'b10;  // AND_Gate and_5, 2 bits wide
  // OR_Gate or_2 has open pins: in0={2{and_3_out[1]}}, in1=and_5_out, out=open
endmodule
