// Logisim project mano_softwareCU.circ as structural Verilog: 10 circuits, main circuit main
module main (
  output [10:0] AR_out,
  output [15:0] PC_out,
  output [15:0] Mem_out,
  output [15:0] DR_out,
  output [6:0] CU_MAP,
  output [15:0] ALU_out,
  output [15:0] AC_out
);

  wire AC_Z, ACTDR, ADD, ALU_AND, ALU_OR, ALU_XOR, ARTPC, CLK, CLRAC, COM, Cout, DRTAC, DRTAR, INCAC, INCDR,
       INCPC, or_1_out, or_2_out, or_3_out, or_4_out, PCTAR, PCTDR, READ, SHL, SHR, SUB, WRITE;
  wire [1:0] priority_encoder_1_out;
  wire [15:0] multiplexer_1_out, multiplexer_2_out;

  Clock clock_1 (.out(CLK));
  Multiplexer #(.width(16)) multiplexer_1 (
    .in0(PC_out), .in1({DR_out[15], CU_MAP[6:3], DR_out[10:0]}), .out(multiplexer_1_out), .sel(DRTAR));
  or or_1 (or_1_out, DRTAR, PCTAR);
  Contrrol_Unit Contrrol_Unit_1 (
    .DR_MAP({CU_MAP[6:3], 3'b000}), .DR_15(DR_out[15]), .Cout(Cout), .AC_Zero(AC_Z), .CLK(CLK), .ADD(ADD),
    .CLRAC(CLRAC), .INCAC(INCAC), .DRTAC(DRTAC), .DRTAR(DRTAR), .PCTAR(PCTAR), .WRITE(WRITE), .SUB(SUB),
    .ALU_OR(ALU_OR), .ALU_AND(ALU_AND), .READ(READ), .ACTDR(ACTDR), .INCDR(INCDR), .PCTDR(PCTDR),
    .ALU_XOR(ALU_XOR), .COM(COM), .SHL(SHL), .SHR(SHR), .INCPC(INCPC), .ARTPC(ARTPC));
  AR AR_1 (.AR_in(multiplexer_1_out), .Load(or_1_out), .CLK(CLK), .AR_out(AR_out));  // open: Inc, Clear
  PC PC_1 (.AR_in(AR_out), .Load(ARTPC), .Inc(INCPC), .CLK(CLK), .PC_out(PC_out));  // open: Clear
  or or_2 (or_2_out, READ, ACTDR, PCTDR);
  Priority_Encoder #(.select(2)) priority_encoder_1 (
    .in0(PCTDR), .in1(READ), .in2(ACTDR), .out(priority_encoder_1_out), .en_in(1'b1));  // open: in3, gs, en_out
  RAM #(.addrWidth(11), .dataWidth(16), .trigger("falling")) RAM_1 (
    .addr(AR_out), .we(WRITE), .oe(READ), .clk(CLK), .din({DR_out[15], CU_MAP[6:3], DR_out[10:0]}),
    .dout(Mem_out));
  or or_3 (or_3_out, ADD, SUB);
  Multiplexer #(.select(2), .width(16)) multiplexer_2 (
    .in0(PC_out), .in1(Mem_out), .in2(AC_out), .out(multiplexer_2_out), .sel(priority_encoder_1_out));  // open: in3
  DR DR_1 (
    .Bus_in(multiplexer_2_out), .Load(or_2_out), .Inc(INCDR), .CLK(CLK),
    .DR_out({DR_out[15], CU_MAP[6:3], DR_out[10:0]}));  // open: Clear
  ALU ALU_1 (
    .A({DR_out[15], CU_MAP[6:3], DR_out[10:0]}), .B(AC_out), .Cin(SUB), .Add_mode(SUB), .AND_PIN(ALU_AND),
    .OR_pin(ALU_OR), .ADD(or_3_out), .T(DRTAC), .XOR_pin(ALU_XOR), .COM(COM), .Res(ALU_out), .out_12(Cout));
  or or_4 (or_4_out, SUB, ADD, ALU_OR, ALU_AND, ALU_XOR, COM, DRTAC);
  AC AC_1 (
    .ALU_in(ALU_out), .Load(or_4_out), .Inc(INCAC), .SHL(SHL), .SHR(SHR), .CLK(CLK), .Clear(CLRAC),
    .AC_out(AC_out));
  Comparator #(.width(16)) comparator_1 (.a({16{1'b0}}), .b(AC_out), .eq(AC_Z));  // open: gt, lt

  assign CU_MAP[2:0] = 3'b000;
  assign DR_out[14:11] = CU_MAP[6:3];
endmodule

module Contrrol_Unit (
  input  [6:0] DR_MAP,
  input  DR_15,
  input  Cout,
  input  AC_Zero,
  input  CLK,
  output ADD,
  output CLRAC,
  output INCAC,
  output DRTAC,
  output DRTAR,
  output PCTAR,
  output WRITE,
  output SUB,
  output ALU_OR,
  output ALU_AND,
  output READ,
  output ACTDR,
  output INCDR,
  output PCTDR,
  output ALU_XOR,
  output COM,
  output SHL,
  output SHR,
  output INCPC,
  output ARTPC
);

  wire Control_unit_branch_logic_1_sbr_l, decoder_3_out7, multiplexer_1_out;
  wire [1:0] BR, CD, Control_unit_branch_logic_1_z0;
  wire [2:0] F1, F2, F3;
  wire [6:0] adder_1_out, CAR_1_car_out, multiplexer_2_out, ROM_1_data, SBR_1_sbr_out;

  Multiplexer #(.select(2)) multiplexer_1 (
    .in0(1'b1), .in1(DR_15), .in2(Cout), .in3(AC_Zero), .out(multiplexer_1_out), .sel(CD));
  Decoder #(.enable("false"), .select(3)) decoder_1 (
    .out1(ADD), .out2(CLRAC), .out3(INCAC), .out4(DRTAC), .out5(DRTAR), .out6(PCTAR), .out7(WRITE), .sel(F1));  // open: out0
  Decoder #(.enable("false"), .select(3)) decoder_2 (
    .out1(SUB), .out2(ALU_OR), .out3(ALU_AND), .out4(READ), .out5(ACTDR), .out6(INCDR), .out7(PCTDR), .sel(F2));  // open: out0
  Decoder #(.enable("false"), .select(3)) decoder_3 (
    .out1(ALU_XOR), .out2(COM), .out3(SHL), .out4(SHR), .out5(INCPC), .out6(ARTPC), .out7(decoder_3_out7),
    .sel(F3));  // open: out0
  Control_unit_branch_logic Control_unit_branch_logic_1 (
    .BR(BR), .test(multiplexer_1_out), .z0(Control_unit_branch_logic_1_z0[0]),
    .z1(Control_unit_branch_logic_1_z0[1]), .SBR_L(Control_unit_branch_logic_1_sbr_l));
  ROM #(.addrWidth(7), .dataWidth(20)) ROM_1 (.addr(CAR_1_car_out), .data({F1, F2, F3, CD, BR, ROM_1_data}));
  Multiplexer #(.select(2), .width(7)) multiplexer_2 (
    .in0(adder_1_out), .in1(ROM_1_data), .in2(SBR_1_sbr_out), .in3(DR_MAP), .out(multiplexer_2_out),
    .sel(Control_unit_branch_logic_1_z0));
  CAR CAR_1 (.CAR_in(multiplexer_2_out), .Load(1'b1), .CLK(CLK), .CAR_out(CAR_1_car_out));
  Adder #(.width(7)) adder_1 (.a(CAR_1_car_out), .b(7'b0000001), .out(adder_1_out));  // open: cin, cout
  SBR SBR_1 (.SBR_in(adder_1_out), .Load(Control_unit_branch_logic_1_sbr_l), .CLK(CLK), .SBR_out(SBR_1_sbr_out));

  // Notes on the sheet:
  //   contents of ROM_1 (hex, n*v repeats v):
  //   2d3 10002 20050 50 4*0 40a 50 2d3 3050 4*0 2d3 14012 e0050 50 4*0 2d3 2001a 9401b e0050 4*0 2d3
  //   10022 c050 50 4*0 2d3 3050 6*0 2d3 1c032 e0033 10034 18035 a0036 3050 0 2d3 1003a 1803b 9403c 9463d
  //   e0050 0 0 2d3 10042 80050 5*0 2d3 44b 50 3050 4*0 c0051 12852 a0180 10055 a0100 0 0 0 2d3 45b 3050
  //   50 4*0 2d3 663 50 3050 4*0 2d3 66b 50 3050 4*0 2d3 10072 4050
endmodule

module PC (
  input  [10:0] AR_in,
  input  Load,
  input  Inc,
  input  CLK,
  input  Clear,
  output [15:0] PC_out
);

  wire or_1_out;
  wire [10:0] adder_1_out, multiplexer_1_out;

  or or_1 (or_1_out, Load, Inc);
  Multiplexer #(.width(11)) multiplexer_1 (.in0(AR_in), .in1(adder_1_out), .out(multiplexer_1_out), .sel(Inc));
  Register #(.width(11)) register_1 (.D(multiplexer_1_out), .en(or_1_out), .clk(CLK), .Q(PC_out[10:0]), .clr(Clear));
  Adder #(.width(11)) adder_1 (.a(11'h1), .b(PC_out[10:0]), .out(adder_1_out));  // open: cin, cout

  assign PC_out[15:11] = {5{1'b0}};
endmodule

module AR (
  input  [15:0] AR_in,
  input  Load,
  input  Inc,
  input  CLK,
  input  Clear,
  output [10:0] AR_out
);

  wire or_1_out;
  wire [10:0] adder_1_out, multiplexer_1_out;

  or or_1 (or_1_out, Load, Inc);
  Multiplexer #(.width(11)) multiplexer_1 (.in0(AR_in[10:0]), .in1(adder_1_out), .out(multiplexer_1_out), .sel(Inc));
  Register #(.width(11)) register_1 (.D(multiplexer_1_out), .en(or_1_out), .clk(CLK), .Q(AR_out), .clr(Clear));
  Adder #(.width(11)) adder_1 (.a(11'h1), .b(AR_out), .out(adder_1_out));  // open: cin, cout
endmodule

module DR (
  input  [15:0] Bus_in,
  input  Load,
  input  Inc,
  input  CLK,
  input  Clear,
  output [15:0] DR_out
);

  wire or_1_out;
  wire [15:0] adder_1_out, multiplexer_1_out;

  or or_1 (or_1_out, Load, Inc);
  Multiplexer #(.width(16)) multiplexer_1 (.in0(Bus_in), .in1(adder_1_out), .out(multiplexer_1_out), .sel(Inc));
  Register #(.width(16)) register_1 (.D(multiplexer_1_out), .en(or_1_out), .clk(CLK), .Q(DR_out), .clr(Clear));
  Adder #(.width(16)) adder_1 (.a(16'h1), .b(DR_out), .out(adder_1_out));  // open: cin, cout
endmodule

module ALU (
  input  [15:0] A,
  input  [15:0] B,
  input  Cin,
  input  Add_mode,
  input  AND_PIN,
  input  OR_pin,
  input  ADD,
  input  T,
  input  XOR_pin,
  input  COM,
  output [15:0] Res,
  output out_12
);

  wire [2:0] priority_encoder_1_out;
  wire [15:0] adder_1_out, and_1_out, multiplexer_1_out, not_1_out, not_2_out, or_1_out, xor_1_out;

  assign not_1_out = ~B;  // NOT_Gate not_1, 16 bits wide
  Multiplexer #(.width(16)) multiplexer_1 (.in0(B), .in1(not_1_out), .out(multiplexer_1_out), .sel(Add_mode));
  assign and_1_out = A & B;  // AND_Gate and_1, 16 bits wide
  assign or_1_out = A | B;  // OR_Gate or_1, 16 bits wide
  Adder #(.width(16)) adder_1 (.a(A), .b(multiplexer_1_out), .out(adder_1_out), .cin(Cin), .cout(out_12));
  assign xor_1_out = A ^ B;  // XOR_Gate xor_1, 16 bits wide
  assign not_2_out = ~B;  // NOT_Gate not_2, 16 bits wide
  Priority_Encoder priority_encoder_1 (
    .in0(AND_PIN), .in1(OR_pin), .in2(ADD), .in3(T), .in4(XOR_pin), .in5(COM), .out(priority_encoder_1_out),
    .en_in(1'b1));  // open: in6, in7, gs, en_out
  Multiplexer #(.select(3), .width(16)) multiplexer_2 (
    .in0(and_1_out), .in1(or_1_out), .in2(adder_1_out), .in3(A), .in4(xor_1_out), .in5(not_2_out), .out(Res),
    .sel(priority_encoder_1_out));  // open: in6, in7
endmodule

module AC (
  input  [15:0] ALU_in,
  input  Load,
  input  Inc,
  input  SHL,
  input  SHR,
  input  CLK,
  input  Clear,
  output [15:0] AC_out
);

  wire or_1_out;
  wire [1:0] priority_encoder_1_out;
  wire [15:0] adder_1_out, multiplexer_1_out, shifter_1_out, shifter_2_out;

  or or_1 (or_1_out, Load, Inc, SHL, SHR);
  Priority_Encoder #(.select(2)) priority_encoder_1 (
    .in0(Load), .in1(Inc), .in2(SHL), .in3(SHR), .out(priority_encoder_1_out), .en_in(1'b1));  // open: gs, en_out
  Multiplexer #(.select(2), .width(16)) multiplexer_1 (
    .in0(ALU_in), .in1(adder_1_out), .in2(shifter_1_out), .in3(shifter_2_out), .out(multiplexer_1_out),
    .sel(priority_encoder_1_out));
  Register #(.width(16)) register_1 (.D(multiplexer_1_out), .en(or_1_out), .clk(CLK), .Q(AC_out), .clr(Clear));
  Adder #(.width(16)) adder_1 (.a(16'h1), .b(AC_out), .out(adder_1_out));  // open: cin, cout
  Shifter #(.width(16)) shifter_1 (.in(AC_out), .\dist (4'b0001), .out(shifter_1_out));
  Shifter #(.shift("lr"), .width(16)) shifter_2 (.\dist (4'b0001), .out(shifter_2_out));  // open: in
endmodule

module CAR (
  input  [6:0] CAR_in,
  input  Load,
  input  CLK,
  output [6:0] CAR_out
);

  Register #(.width(7)) register_1 (.D(CAR_in), .en(Load), .clk(CLK), .Q(CAR_out));  // open: clr
endmodule

module SBR (
  input  [6:0] SBR_in,
  input  Load,
  input  CLK,
  output [6:0] SBR_out
);

  Register #(.width(7)) register_1 (.D(SBR_in), .en(Load), .clk(CLK), .Q(SBR_out));  // open: clr
endmodule

module Control_unit_branch_logic (
  input  [1:0] BR,
  input  test,
  output z0,
  output z1,
  output SBR_L
);

  wire and_1_out, and_2_out;

  and and_1 (and_1_out, BR[0], BR[1]);
  and and_2 (and_2_out, ~BR[1], test);  // AND_Gate
  and and_3 (SBR_L, ~BR[1], BR[0], test);  // AND_Gate
  or or_1 (z0, and_1_out, and_2_out);

  assign z1 = BR[1];
endmodule
